// Logisim project 4bt ALU.circ as structural Verilog: 3 circuits, main circuit main
module main (
  input  [3:0] A,
  input  [3:0] B,
  input  [3:0] OPCODE,
  output Overflow,
  output Z,
  output C,
  output N,
  output [3:0] Y
);

  wire [3:0] AU_out, LU_out, multiplexer_1_out, multiplexer_2_out, not_1_out, not_2_out;

  Multiplexer #(.width(4), .enable("false")) multiplexer_1 (
    .in0(A), .in1(not_1_out), .out(multiplexer_1_out), .sel(OPCODE[0]));
  assign not_1_out = ~A;  // NOT_Gate not_1, 4 bits wide
  Multiplexer #(.width(4), .enable("false")) multiplexer_2 (
    .in0(B), .in1(not_2_out), .out(multiplexer_2_out), .sel(OPCODE[1]));
  assign not_2_out = ~B;  // NOT_Gate not_2, 4 bits wide
  Au AU (.cin(OPCODE[2]), .A(multiplexer_1_out), .B(multiplexer_2_out), .OUT(AU_out), .overflow(Overflow), .cout(C));
  lu LU (.A(A), .B(multiplexer_2_out), .f2(OPCODE[2]), .f0(OPCODE[0]), .OUT(LU_out));
  Multiplexer #(.width(4), .enable("false")) multiplexer_3 (
    .in0(AU_out), .in1(LU_out), .out({N, Y[2:0]}), .sel(OPCODE[3]));
  nor nor_1 (Z, Y[0], Y[1], Y[2], N);

  assign Y[3] = N;
endmodule

module Au (
  input  cin,
  input  [3:0] A,
  input  [3:0] B,
  output [3:0] OUT,
  output overflow,
  output cout
);

  wire adder_1_cout, adder_2_cout, adder_3_cout;

  Adder #(.width(1)) adder_1 (.a(A[0]), .b(B[0]), .out(OUT[0]), .cin(cin), .cout(adder_1_cout));
  Adder #(.width(1)) adder_2 (.a(A[1]), .b(B[1]), .out(OUT[1]), .cin(adder_1_cout), .cout(adder_2_cout));
  Adder #(.width(1)) adder_3 (.a(A[2]), .b(B[2]), .out(OUT[2]), .cin(adder_2_cout), .cout(adder_3_cout));
  Adder #(.width(1)) adder_4 (.a(A[3]), .b(B[3]), .out(OUT[3]), .cin(adder_3_cout), .cout(cout));
  xor xor_1 (overflow, adder_3_cout, cout);
endmodule

module lu (
  input  [3:0] A,
  input  [3:0] B,
  input  f2,
  input  f0,
  output [3:0] OUT
);

  wire [3:0] and_1_out, or_1_out, xor_1_out;

  assign and_1_out = A & B;  // AND_Gate and_1, 4 bits wide
  assign or_1_out = A | B;  // OR_Gate or_1, 4 bits wide
  assign xor_1_out = A ^ B;  // XOR_Gate xor_1, 4 bits wide
  Multiplexer #(.select(2), .width(4), .enable("false")) multiplexer_1 (
    .in0(and_1_out), .in1(or_1_out), .in2(xor_1_out), .in3(B), .out(OUT), .sel({f2, f0}));
endmodule
